// Logisim project Test_Circuits.circ as structural Verilog: 1 circuit, main circuit main
module main (
  input  A,
  input  A_2,
  input  B,
  input  B_2,
  input  C,
  input  A_3,
  input  A_4,
  input  B_3,
  input  B_4,
  input  C_2,
  input  A_5,
  input  B_5,
  input  C_3,
  output out_14,
  output out_15,
  output out_16,
  output out_17,
  output out_18
);

  wire and_2_out, not_1_out, or_1_out;

  and and_1 (out_16, A_4, B_4);
  and and_2 (and_2_out, B_2, C);
  or or_1 (or_1_out, A_5, B_5);
  or or_2 (out_14, A, and_2_out);
  and and_3 (out_18, or_1_out, C_3);
  not not_1 (not_1_out, A_2);
  xor xor_1 (out_15, not_1_out, B);
  nand nand_1 (out_17, A_3, B_3, C_2);

  // Notes on the sheet:
  //   Circuit 2
  //   Circuit 1
  //   Circuit 3
  //   Circuit 4
  //   Circuit 5
endmodule
